// Logisim project Final_Project_CPU.circ as structural Verilog: 3 circuits, main circuit CPU_main
module CPU_main (
  input  reset
);

  wire clk, DWE, SUB, WE;
  wire [1:0] AFS, RSS;
  wire [2:0] AddrA, AddrB, AddrD, lab9_register_file_main_1_porta_2;
  wire [3:0] lab6_alu_main_1_alu_out, lab9_register_file_main_1_portb, multiplexer_1_out;
  wire [3:3] lab9_register_file_main_1_porta;
  wire [7:0] counter_1_q;
  wire [15:3] rom_1_data;

  Clock u_clk (.out(clk));
  Counter counter_1 (.clr(reset), .load(1'b0), .up(1'b1), .count(1'b1), .clk(clk), .Q(counter_1_q));  // open: D, carry
  ROM #(.dataWidth(16)) rom_1 (
    .addr(counter_1_q), .data({rom_1_data[15:11], AddrD, rom_1_data[7], AddrA, rom_1_data[3], AddrB}));
  ROM #(.addrWidth(4), .dataWidth(7)) rom_2 (.addr(rom_1_data[15:12]), .data({SUB, AFS, RSS, DWE, WE}));
  Multiplexer #(.select(2), .width(4)) multiplexer_1 (
    .in0({rom_1_data[3], AddrB}), .in1(lab6_alu_main_1_alu_out),
    .in2({lab9_register_file_main_1_porta[3], lab9_register_file_main_1_porta_2}), .out(multiplexer_1_out),
    .sel(RSS));  // open: in3
  Lab9_Register_File_main lab9_register_file_main_1 (
    .WE(WE), .WAddr(AddrD), .RAddrA(AddrA), .RAddrB(AddrB), .PortD(multiplexer_1_out), .Clk(clk),
    .PortA({lab9_register_file_main_1_porta[3], lab9_register_file_main_1_porta_2}),
    .PortB(lab9_register_file_main_1_portb));
  TTY tty_1 (
    .data({lab9_register_file_main_1_porta_2, lab9_register_file_main_1_portb}), .clk(clk), .we(DWE),
    .clr(reset));
  Lab6_ALU_main lab6_alu_main_1 (
    .A({lab9_register_file_main_1_porta[3], lab9_register_file_main_1_porta_2}),
    .B(lab9_register_file_main_1_portb), .AFS(AFS), .SUB(SUB), .ALU_OUT(lab6_alu_main_1_alu_out));

  // Notes on the sheet:
  //   contents of rom_1 (hex, n*v repeats v):
  //   1704 1402 3074 1507 3054 1306 120f 3032 3037 3054 1609 3036 1103 3031 1000 3040 1005 3006 3032 3050
  //   100e 3030 3035 1000 3040 3041 1001 3010 3011 1600 150a 3065 3017 120b 3042 3014 100d 3010 7374 3013
  //   3065 3017 3045 3014 3010 7377 3013 3065 3017 3040 3014 3010 120f 4024 1201 7302 7437 3014 3065 3017
  //   3040 3014 3010 f374 3013
  //   contents of rom_2 (hex, n*v repeats v):
  //   0 1 9 2 5 15 25 35 7*0 75
endmodule

module Lab9_Register_File_main (
  input  WE,
  input  [2:0] WAddr,
  input  [2:0] RAddrA,
  input  [2:0] RAddrB,
  input  [3:0] PortD,
  input  Clk,
  output [3:0] PortA,
  output [3:0] PortB
);

  wire decoder_1_out0, decoder_1_out1, decoder_1_out2, decoder_1_out3, decoder_1_out4, decoder_1_out5,
       decoder_1_out6, decoder_1_out7;
  wire [3:0] D0, D1, D2, D3, D4, D5, D6, D7;

  Decoder #(.select(3)) decoder_1 (
    .out0(decoder_1_out0), .out1(decoder_1_out1), .out2(decoder_1_out2), .out3(decoder_1_out3),
    .out4(decoder_1_out4), .out5(decoder_1_out5), .out6(decoder_1_out6), .out7(decoder_1_out7), .sel(WAddr),
    .en(WE));
  Four_bit_register four_bit_register_1 (.Din(PortD), .Write_EN(decoder_1_out0), .Clk(Clk), .Dout(D0));
  Four_bit_register four_bit_register_2 (.Din(PortD), .Write_EN(decoder_1_out1), .Clk(Clk), .Dout(D1));
  Four_bit_register four_bit_register_3 (.Din(PortD), .Write_EN(decoder_1_out2), .Clk(Clk), .Dout(D2));
  Four_bit_register four_bit_register_4 (.Din(PortD), .Write_EN(decoder_1_out3), .Clk(Clk), .Dout(D3));
  Four_bit_register four_bit_register_5 (.Din(PortD), .Write_EN(decoder_1_out4), .Clk(Clk), .Dout(D4));
  Four_bit_register four_bit_register_6 (.Din(PortD), .Write_EN(decoder_1_out5), .Clk(Clk), .Dout(D5));
  Four_bit_register four_bit_register_7 (.Din(PortD), .Write_EN(decoder_1_out6), .Clk(Clk), .Dout(D6));
  Four_bit_register four_bit_register_8 (.Din(PortD), .Write_EN(decoder_1_out7), .Clk(Clk), .Dout(D7));
  Multiplexer #(.select(3), .width(4)) multiplexer_1 (
    .in0(D0), .in1(D1), .in2(D2), .in3(D3), .in4(D4), .in5(D5), .in6(D6), .in7(D7), .out(PortA), .sel(RAddrA));
  Multiplexer #(.select(3), .width(4)) multiplexer_2 (
    .in0(D0), .in1(D1), .in2(D2), .in3(D3), .in4(D4), .in5(D5), .in6(D6), .in7(D7), .out(PortB), .sel(RAddrB));

  // Notes on the sheet:
  //   Brodric Young
endmodule

module Four_bit_register (
  input  [3:0] Din,
  input  Write_EN,
  input  Clk,
  output [3:0] Dout
);

  wire multiplexer_1_out, multiplexer_2_out, multiplexer_3_out, multiplexer_4_out;

  D_Flip_Flop d_ff_1 (.D(multiplexer_1_out), .clk(Clk), .Q(Dout[3]));  // open: Qn, preset, reset
  Multiplexer multiplexer_1 (.in0(Dout[3]), .in1(Din[3]), .out(multiplexer_1_out), .sel(Write_EN));
  D_Flip_Flop d_ff_2 (.D(multiplexer_2_out), .clk(Clk), .Q(Dout[2]));  // open: Qn, preset, reset
  Multiplexer multiplexer_2 (.in0(Dout[2]), .in1(Din[2]), .out(multiplexer_2_out), .sel(Write_EN));
  D_Flip_Flop d_ff_3 (.D(multiplexer_3_out), .clk(Clk), .Q(Dout[1]));  // open: Qn, preset, reset
  Multiplexer multiplexer_3 (.in0(Dout[1]), .in1(Din[1]), .out(multiplexer_3_out), .sel(Write_EN));
  D_Flip_Flop d_ff_4 (.D(multiplexer_4_out), .clk(Clk), .Q(Dout[0]));  // open: Qn, preset, reset
  Multiplexer multiplexer_4 (.in0(Dout[0]), .in1(Din[0]), .out(multiplexer_4_out), .sel(Write_EN));

  // Other names for the same wires on the sheet: w_e = Write_EN

  // Notes on the sheet:
  //   Brodric Young
endmodule
