// Logisim project Lab6_ALU.circ as structural Verilog: 9 circuits, main circuit Lab6_ALU_main
module Lab6_ALU_main (
  input  [3:0] A,
  input  [3:0] B,
  input  [1:0] AFS,
  input  SUB,
  output [3:0] ALU_OUT
);

  wire [3:0] add_or_sub_4bit_1_result, and_4bit_1_and4, or_4bit_1_or4, xor_4bit_1_xor4;

  Add_or_Sub_4bit add_or_sub_4bit_1 (.A(A), .B(B), .SUB(SUB), .Result(add_or_sub_4bit_1_result));
  XOR_4bit xor_4bit_1 (.A(A), .B(B), .XOR4(xor_4bit_1_xor4));
  OR_4bit or_4bit_1 (.A(A), .B(B), .OR4(or_4bit_1_or4));
  AND_4bit and_4bit_1 (.A(A), .B(B), .AND4(and_4bit_1_and4));
  MUX4to1_4bit mux4to1_4bit_1 (
    .IN0(xor_4bit_1_xor4), .IN2(or_4bit_1_or4), .IN1(and_4bit_1_and4), .IN3(add_or_sub_4bit_1_result),
    .S(AFS), .MUX_out(ALU_OUT));

  // Notes on the sheet:
  //   Brodric Young
endmodule

module MUX2to1_1bit (
  input  A,
  input  B,
  input  S,
  output F
);

  wire and_1_out, and_2_out, not_1_out;

  not not_1 (not_1_out, S);
  and and_1 (and_1_out, A, not_1_out);
  and and_2 (and_2_out, B, S);
  or or_1 (F, and_1_out, and_2_out);
endmodule

module MUX2to1_4bit (
  input  [3:0] A,
  input  [3:0] B,
  input  S,
  output [3:0] F
);

  MUX2to1_1bit mux2to1_1bit_1 (.A(A[3]), .B(B[3]), .S(S), .F(F[3]));
  MUX2to1_1bit mux2to1_1bit_2 (.A(A[2]), .B(B[2]), .S(S), .F(F[2]));
  MUX2to1_1bit mux2to1_1bit_3 (.A(A[1]), .B(B[1]), .S(S), .F(F[1]));
  MUX2to1_1bit mux2to1_1bit_4 (.A(A[0]), .B(B[0]), .S(S), .F(F[0]));
endmodule

module Full_Adder (
  input  A,
  input  B,
  input  Cin,
  output S,
  output Cout
);

  wire and_1_out, and_2_out, and_3_out;

  and and_1 (and_1_out, A, B);
  and and_2 (and_2_out, A, Cin);
  and and_3 (and_3_out, B, Cin);
  xor xor_1 (S, A, B, Cin);
  or or_1 (Cout, and_1_out, and_2_out, and_3_out);
endmodule

module AND_4bit (
  input  [3:0] A,
  input  [3:0] B,
  output [3:0] AND4
);

  and and_1 (AND4[3], A[3], B[3]);
  and and_2 (AND4[2], A[2], B[2]);
  and and_3 (AND4[1], A[1], B[1]);
  and and_4 (AND4[0], A[0], B[0]);
endmodule

module OR_4bit (
  input  [3:0] A,
  input  [3:0] B,
  output [3:0] OR4
);

  or or_1 (OR4[3], A[3], B[3]);
  or or_2 (OR4[2], A[2], B[2]);
  or or_3 (OR4[1], A[1], B[1]);
  or or_4 (OR4[0], A[0], B[0]);
endmodule

module XOR_4bit (
  input  [3:0] A,
  input  [3:0] B,
  output [3:0] XOR4
);

  xor xor_1 (XOR4[3], A[3], B[3]);
  xor xor_2 (XOR4[2], A[2], B[2]);
  xor xor_3 (XOR4[1], A[1], B[1]);
  xor xor_4 (XOR4[0], A[0], B[0]);
endmodule

module MUX4to1_4bit (
  input  [3:0] IN0,
  input  [3:0] IN2,
  input  [3:0] IN1,
  input  [3:0] IN3,
  input  [1:0] S,
  output [3:0] MUX_out
);

  wire [3:0] mux2to1_4bit_1_f, mux2to1_4bit_2_f;

  MUX2to1_4bit mux2to1_4bit_1 (.A(IN0), .B(IN2), .S(S[1]), .F(mux2to1_4bit_1_f));
  MUX2to1_4bit mux2to1_4bit_2 (.A(IN1), .B(IN3), .S(S[1]), .F(mux2to1_4bit_2_f));
  MUX2to1_4bit mux2to1_4bit_3 (.A(mux2to1_4bit_1_f), .B(mux2to1_4bit_2_f), .S(S[0]), .F(MUX_out));

  // Notes on the sheet:
  //   (A input)
  //   (C input)
  //   (B input)
  //   (D input)
  //   Brodric Young
  //   (F)
endmodule

module Add_or_Sub_4bit (
  input  [3:0] A,
  input  [3:0] B,
  input  SUB,
  output [3:0] Result
);

  wire full_adder_2_cout, full_adder_3_cout, full_adder_4_cout, xor_1_out, xor_2_out, xor_3_out, xor_4_out;

  xor xor_1 (xor_1_out, B[3], SUB);
  xor xor_2 (xor_2_out, B[2], SUB);
  xor xor_3 (xor_3_out, B[1], SUB);
  xor xor_4 (xor_4_out, B[0], SUB);
  Full_Adder full_adder_1 (.A(A[3]), .B(xor_1_out), .Cin(full_adder_2_cout), .S(Result[3]));  // open: Cout
  Full_Adder full_adder_2 (.A(A[2]), .B(xor_2_out), .Cin(full_adder_3_cout), .S(Result[2]), .Cout(full_adder_2_cout));
  Full_Adder full_adder_3 (.A(A[1]), .B(xor_3_out), .Cin(full_adder_4_cout), .S(Result[1]), .Cout(full_adder_3_cout));
  Full_Adder full_adder_4 (.A(A[0]), .B(xor_4_out), .Cin(SUB), .S(Result[0]), .Cout(full_adder_4_cout));

  // Other names for the same wires on the sheet: S0 = Result[0]; S1 = Result[1]; S2 = Result[2]; S3 = Result[3]

  // Notes on the sheet:
  //   Brodric Young
endmodule
