// Logisim project Ring_Counter.circ as structural Verilog: 1 circuit, main circuit main
module main (
  input  Reset,
  output Q2,
  output Q1,
  output Q0
);

  wire clk;

  Clock u_clk (.out(clk));
  Clock sysclk ();  // open: out
  D_Flip_Flop d_ff_1 (.D(Q1), .clk(clk), .Q(Q2), .reset(Reset));  // open: Qn, preset
  D_Flip_Flop d_ff_2 (.D(Q0), .clk(clk), .Q(Q1), .reset(Reset));  // open: Qn, preset
  D_Flip_Flop d_ff_3 (.D(Q2), .clk(clk), .Q(Q0), .preset(Reset));  // open: Qn, reset

  // Notes on the sheet:
  //   Brodric Young
endmodule
