// Logisim project RoadRipper.circ as structural Verilog: 1 circuit, main circuit main
module main (
  input  Right,
  input  Stop,
  input  Clock,
  input  Left,
  output L_Back,
  output R_Front,
  output L_Front,
  output R_Back
);

  wire and_3_out, and_4_out, and_5_out, and_6_out, not_1_out, not_2_out, or_1_out, or_2_out;

  not not_1 (not_1_out, Right);
  and and_1 (R_Front, Right, Clock);
  and and_2 (L_Front, Clock, Left);
  not not_2 (not_2_out, Left);
  and and_3 (and_3_out, Stop, Right);
  and and_4 (and_4_out, Stop, not_1_out);
  and and_5 (and_5_out, not_2_out, Stop);
  and and_6 (and_6_out, Left, Stop);
  or or_1 (or_1_out, and_4_out, R_Front);
  or or_2 (or_2_out, L_Front, and_5_out);
  or or_3 (L_Back, and_3_out, or_2_out);
  or or_4 (R_Back, or_1_out, and_6_out);

  // Notes on the sheet:
  //   Brodric Young
endmodule
