// Logisim project Lab8_Latches_and_FlipFlops.circ as structural Verilog: 6 circuits, main circuit main
module main (
  input  S_NOR,
  input  R_NOR,
  input  Sn_NAND,
  input  Rn_NAND,
  input  D,
  input  Gate,
  output Qn_NOR,
  output Q_NOR,
  output Q_NAND,
  output Qn_NAND,
  output Qn_GateD,
  output Q_GateD
);

  wire and_1_out, and_2_out, not_1_out;

  not not_1 (not_1_out, D);
  nor nor_1 (Qn_NOR, S_NOR, Q_NOR);
  nor nor_2 (Q_NOR, Qn_NOR, R_NOR);
  and and_1 (and_1_out, D, Gate);
  and and_2 (and_2_out, not_1_out, Gate);
  nand nand_1 (Q_NAND, Sn_NAND, Qn_NAND);
  nand nand_2 (Qn_NAND, Q_NAND, Rn_NAND);
  nor nor_3 (Qn_GateD, and_1_out, Q_GateD);
  nor nor_4 (Q_GateD, Qn_GateD, and_2_out);

  // Notes on the sheet:
  //   NOR Latch
  //   NAND Latch
  //   Gated D Latch
  //   Brodric Young
endmodule

module NOR_SR_Latch (
  input  S_NOR,
  input  R_NOR,
  output Qn_NOR,
  output Q_NOR
);

  nor nor_1 (Qn_NOR, S_NOR, Q_NOR);
  nor nor_2 (Q_NOR, Qn_NOR, R_NOR);

  // Notes on the sheet:
  //   Brodric Young
endmodule

module NAND_SR_Latch (
  input  Sn_NAND,
  input  Rn_NAND,
  output Q_NAND,
  output Qn_NAND
);

  wire not_1_out, not_2_out;

  not not_1 (not_1_out, Sn_NAND);
  not not_2 (not_2_out, Rn_NAND);
  nand nand_1 (Q_NAND, not_1_out, Qn_NAND);
  nand nand_2 (Qn_NAND, Q_NAND, not_2_out);

  // Notes on the sheet:
  //   Brodric Young
endmodule

module Gated_D_Latch (
  input  D,
  input  Gate,
  output Qn_GateD,
  output Q_GateD
);

  wire and_1_out, and_2_out, not_1_out;

  not not_1 (not_1_out, D);
  and and_1 (and_1_out, D, Gate);
  and and_2 (and_2_out, not_1_out, Gate);
  nor nor_1 (Qn_GateD, and_1_out, Q_GateD);
  nor nor_2 (Q_GateD, Qn_GateD, and_2_out);

  // Notes on the sheet:
  //   Brodric Young
endmodule

module D_ff (
  input  S,
  input  D,
  input  R,
  output Q,
  output Qn
);

  wire clock_1_out;

  D_Flip_Flop d_ff_1 (.D(D), .clk(clock_1_out), .Q(Q), .Qn(Qn), .preset(S), .reset(R));
  Clock clock_1 (.out(clock_1_out));

  // Notes on the sheet:
  //   Flip Flop
endmodule

module D_toggle_ff (
  output D,
  output Q
);

  wire CLK_out;

  not not_1 (D, Q);
  D_Flip_Flop d_ff_1 (.D(D), .clk(CLK_out), .Q(Q));  // open: Qn, preset, reset
  Clock CLK (.out(CLK_out));

  // Notes on the sheet:
  //   Toggle Circuit
endmodule
